# Fritzing sketch Mneme (saved by Fritzing 0.9.2b)
circuit board: 6.88566cm x 5.36311cm
breadboards: 1

parts:
  R5 = Photocell (LDR) [package=THT]
  LED3 = LED - 5mm [color="Red (633nm)" package="5 mm [THT]"]
  R6 = Resistor [tolerance=±5% resistance=10k package=THT]
  Arduino1 = Arduino Uno (Rev3)
  SP1 = SPEAKER [package=pcb_mount_speaker]
  DFPlayer_Mini1 = DFPlayer MINI [package="DIP (Dual Inline) [THT]"]
  R7 = Resistor [tolerance=±5% resistance=1k package=THT]

nets (from the breadboard view):
  5V: R5.pin_0, Arduino1.5V, DFPlayer_Mini1.VCC
  N1: R5.pin_1, R6.Pin_0, Arduino1.A0
  N2: LED3.cathode, Arduino1.D13/SCK
  GND: LED3.anode, R6.Pin_1, Arduino1.GND, DFPlayer_Mini1.GND
  N3: Arduino1.D10_PWM/SS, DFPlayer_Mini1.TX
  N4: Arduino1.D11_PWM/MOSI, R7.Pin_1
  N5: SP1.+, DFPlayer_Mini1.SPK2
  N6: SP1.-, DFPlayer_Mini1.SPK1
  N7: DFPlayer_Mini1.RX, R7.Pin_0

custom parts:
  DFPlayer MINI: MP3 module by DFRobot.com for playing Music from an SD-Card. Supports WAV and MP3 files.

// code stored in the sketch: Untitled3.ino

